# Fritzing sketch Project (saved by Fritzing 0.9.3b)
breadboards: 1

parts:
  Arduino_Uno = Arduino Uno (Rev3)
  LDR = Photocell (LDR) [package=THT]
  Resistor = Resistor [tolerance=±5% resistance=10k package="2512 [SMD]"]
  AC_Power_Source = Lilypad Battery Connect
  Part1 = Bluetooth HC-05 Macho
  R3 = Resistor [tolerance=±5% resistance=1k package="0805 [SMD]"]
  LED3 = LEDs [package=led10mm]
  KY-2 = Keyes Relay [package=THT]
  Sensore_PIR_HC-SR502 = HC-SR501 Body Sensor Module
  R4 = Resistor [tolerance=±5% resistance=3.3k package="0402 [SMD]"]

nets:
  N1: Arduino_Uno.A0, LDR.pin_1, Resistor.Pin_0
  N2: Arduino_Uno.D8, Sensore_PIR_HC-SR502.OUT
  N3: Arduino_Uno.D9_PWM, Part1.TXD
  N4: Arduino_Uno.D10_PWM/SS, R3.Pin_0
  N5: Arduino_Uno.D13/SCK, KY-2.ground
  VCC: Arduino_Uno.5V, LDR.pin_0, Part1.VCC, KY-2.signal, Sensore_PIR_HC-SR502.VCC
  GND: Arduino_Uno.GND, Resistor.Pin_1, Part1.GND, KY-2.power, Sensore_PIR_HC-SR502.GND, R4.Pin_1
  N6: AC_Power_Source.-, LED3.C
  N7: AC_Power_Source.+, KY-2.NO
  N8: Part1.RXD, R3.Pin_1, R4.Pin_0
  N9: LED3.A, KY-2.C

notes:
  Wiring Scheme
  Red - VCC (5V)
  Black - Ground
  White - LDR Sensor
  Purple - PIR Sensor
  Pink - Relay
  Brown&Orange-RX&TX

custom parts:
  LEDs: LEDs Standard schematic elements and footprints for 5mm, 3mm, 1206, and 0603 sized LEDs. 5mm - Spark Fun Electronics SKU : COM-00529 (and others)
  Keyes Relay: The Keyes 5V relay module is suitable for SCM development, home appliance control. It uses a 5V~12V TIL control signal which can control DC / AC signal.
  HC-SR501 Body Sensor Module: Pyroelectric Infrared PIR Motion Sensor Detector Module
